# Fritzing sketch PhoenixArcade (saved by Fritzing 0.6.2b)
breadboards: 3

parts:
  COIN = screw terminal, 3 pins
  CONTROL = screw terminal, 12 pins
  RGB = screw terminal, 4 pins
  ULN2003 = ULN2003A [package="DIP16 [THT]"]
  DISPLAY1 = female pin header, 3 pins [form="♂ (male)"]
  DISPLAY2 = female pin header, 3 pins [form="♂ (male)"]
  U1 = Arduino Mega

nets:
  N1: COIN.pin1, ULN2003.COM_-_Common, U1.VIN
  N2: COIN.pin2, CONTROL.pin2, CONTROL.pin4, CONTROL.pin6, CONTROL.pin8, CONTROL.pin10, CONTROL.pin12, RGB.pin1, ULN2003.0V, DISPLAY1.pin1, DISPLAY2.pin1, U1.GND
  N3: COIN.pin3, U1.D2
  N4: CONTROL.pin1, U1.D13
  N5: CONTROL.pin3, U1.D12
  N6: CONTROL.pin5, U1.D11
  N7: CONTROL.pin7, U1.D10
  N8: CONTROL.pin9, U1.D9
  N9: CONTROL.pin11, U1.D8
  N10: RGB.pin2, ULN2003.Out_3
  N11: RGB.pin3, ULN2003.Out_2
  N12: RGB.pin4, ULN2003.Out_1
  N13: ULN2003.In_1, U1.D3
  N14: ULN2003.In_2, U1.D4
  N15: ULN2003.In_3, U1.D5
  N16: DISPLAY1.pin2, DISPLAY2.pin2, U1.+5V
  N17: DISPLAY1.pin3, U1.D18
  N18: DISPLAY2.pin3, U1.D16

notes:
  Phoenix Arcade v0.1
