# Fritzing sketch PhoenixArcade_v2 (saved by Fritzing 0.6.3b)
breadboards: 2

parts:
  U1 = Arduino Mega
  BUTTONS = female pin header, 7 pins [form="♂ (male)"]
  DISPLAY = female pin header, 4 pins [form="♂ (male)"]
  ULN2003 = ULN2003A [package="DIP16 [THT]"]
  FICHEIRO = screw terminal, 4 pins
  RGB = screw terminal, 4 pins

nets:
  N1: U1.GND, BUTTONS.pin1, DISPLAY.pin2, ULN2003.0V, FICHEIRO.pin2
  N2: U1.D11, ULN2003.In_3
  N3: U1.D10, ULN2003.In_2
  N4: U1.D9, ULN2003.In_1
  N5: U1.D7, BUTTONS.pin2
  N6: U1.D6, BUTTONS.pin3
  N7: U1.D5, BUTTONS.pin4
  N8: U1.D4, BUTTONS.pin5
  N9: U1.D3, BUTTONS.pin6
  N10: U1.D2, BUTTONS.pin7
  N11: U1.VIN, DISPLAY.pin1, ULN2003.COM_-_Common, FICHEIRO.pin1, RGB.pin1
  N12: U1.D18, DISPLAY.pin3
  N13: U1.D19, DISPLAY.pin4
  N14: U1.D30, FICHEIRO.pin4
  N15: ULN2003.Out_3, RGB.pin2
  N16: ULN2003.Out_2, RGB.pin3
  N17: ULN2003.Out_1, RGB.pin4

notes:
  Phoenix Arcade v2
  Phoenix
